// Logisim project 3bitcarry.circ as structural Verilog: 1 circuit, main circuit main
module main (
  input  b_1,
  input  b_2,
  input  b_3,
  output c
);

  wire and_1_out, and_2_out, and_3_out, or_1_out;

  and and_1 (and_1_out, b_3, b_2);
  and and_2 (and_2_out, b_3, b_1);
  and and_3 (and_3_out, b_2, b_1);
  or or_1 (or_1_out, and_1_out, and_2_out);
  or or_2 (c, or_1_out, and_3_out);
endmodule
