// Logisim project AND4.circ as structural Verilog: 2 circuits, main circuit main
module main (
  input  in_1,
  input  in_2,
  input  in_3,
  input  in_4,
  output out_5
);

  wire and_1_out, and_2_out;

  and and_1 (and_1_out, in_1, in_2);
  and and_2 (and_2_out, in_3, in_4);
  and and_3 (out_5, and_1_out, and_2_out);
endmodule

module Circuit1 (
  input  in_1,
  input  in_2,
  input  in_3,
  input  in_4,
  input  in_5,
  input  in_6,
  input  in_7,
  input  in_8,
  output out_9
);

  wire main_1_out_5, main_2_out_5;

  main main_1 (.in_1(in_1), .in_2(in_2), .in_3(in_3), .in_4(in_4), .out_5(main_1_out_5));
  main main_2 (.in_1(in_5), .in_2(in_6), .in_3(in_7), .in_4(in_8), .out_5(main_2_out_5));
  and and_1 (out_9, main_1_out_5, main_2_out_5);
endmodule
