// Logisim project DEC_1.circ as structural Verilog
module DECODER_1 (
  input  in_1,
  output out_2,
  output out_3
);

  not not_1 (out_2, in_1);

  assign out_3 = in_1;
endmodule

module DECODER_2 (
  input  x_0,
  input  x_1,
  output y_1,
  output y_0,
  output y_3,
  output y_2
);

  wire decoder_1_1_out_2, decoder_1_1_out_3, decoder_1_2_out_2, decoder_1_2_out_3;

  DECODER_1 decoder_1_1 (.in_1(x_1), .out_2(decoder_1_1_out_2), .out_3(decoder_1_1_out_3));
  and and_1 (y_1, decoder_1_1_out_2, decoder_1_2_out_3);
  and and_2 (y_3, decoder_1_1_out_3, decoder_1_2_out_3);
  DECODER_1 decoder_1_2 (.in_1(x_0), .out_2(decoder_1_2_out_2), .out_3(decoder_1_2_out_3));
  and and_3 (y_0, decoder_1_1_out_2, decoder_1_2_out_2);
  and and_4 (y_2, decoder_1_1_out_3, decoder_1_2_out_2);
endmodule

module DECODER_3 (
  input  x_1,
  input  x_0,
  input  x_2,
  output y_3,
  output y_2,
  output y_1,
  output y_0,
  output y_7,
  output y_6,
  output y_5,
  output y_4
);

  wire decoder_1_1_out_2, decoder_1_1_out_3, decoder_2_1_y_0, decoder_2_1_y_1, decoder_2_1_y_2,
       decoder_2_1_y_3;

  DECODER_1 decoder_1_1 (.in_1(x_2), .out_2(decoder_1_1_out_2), .out_3(decoder_1_1_out_3));
  and and_1 (y_3, decoder_1_1_out_2, decoder_2_1_y_3);
  and and_2 (y_7, decoder_1_1_out_3, decoder_2_1_y_3);
  DECODER_2 decoder_2_1 (
    .x_1(x_1), .x_0(x_0), .y_1(decoder_2_1_y_1), .y_3(decoder_2_1_y_3), .y_0(decoder_2_1_y_0),
    .y_2(decoder_2_1_y_2));
  and and_3 (y_2, decoder_1_1_out_2, decoder_2_1_y_2);
  and and_4 (y_6, decoder_1_1_out_3, decoder_2_1_y_2);
  and and_5 (y_1, decoder_1_1_out_2, decoder_2_1_y_1);
  and and_6 (y_5, decoder_1_1_out_3, decoder_2_1_y_1);
  and and_7 (y_0, decoder_1_1_out_2, decoder_2_1_y_0);
  and and_8 (y_4, decoder_1_1_out_3, decoder_2_1_y_0);
endmodule
